# Fritzing sketch Schema (saved by Fritzing 0.9.3b)
breadboards: 2

parts:
  Part1 = Arduino Uno (Rev3)
  Disp2 = LBT2088AH [part_number=LBT2088AH]
  R6 = Resistor [tolerance=±5% resistance=220 package="0805 [SMD]"]
  R3 = Resistor [tolerance=±5% resistance=220 package="0805 [SMD]"]
  R7 = Resistor [tolerance=±5% resistance=220 package="0805 [SMD]"]
  R1 = Resistor [tolerance=±5% resistance=220 package="0805 [SMD]"]
  R5 = Resistor [tolerance=±5% resistance=220 package="0805 [SMD]"]
  R4 = Resistor [tolerance=±5% resistance=220 package="0805 [SMD]"]
  R2 = Resistor [tolerance=±5% resistance=220 package="0805 [SMD]"]
  R0 = Resistor [tolerance=±5% resistance=220 package="0805 [SMD]"]
  U1 = 74HC595 [package="DIP16 [THT]"]
  U2 = 74HC595 [package="DIP16 [THT]"]
  Keypad4x2 = Keypad Membran 4x4

nets:
  N1: Part1.D8, Keypad4x2.Pin5
  N2: Part1.D9_PWM, Keypad4x2.Pin4
  N3: Part1.D10_PWM/SS, Keypad4x2.Pin3
  N4: Part1.D11_PWM/MOSI, Keypad4x2.Pin2
  N5: Part1.D12/MISO, Keypad4x2.Pin1
  GND: Part1.GND, U1.GND, U1.OE
  N6: Part1.D2, U2.DS
  N7: Part1.D3_PWM, U1.SH_CP, U2.SH_CP
  N8: Part1.D4, U1.ST_CP, U2.ST_CP
  N9: Part1.D5_PWM, Keypad4x2.Pin8
  N10: Part1.D6_PWM, Keypad4x2.Pin7
  N11: Part1.D7, Keypad4x2.Pin6
  VCC: Part1.5V, U1.MR, U1.VCC, U2.MR, U2.VCC
  N12: Disp2.pin1, U2.Q7
  N13: Disp2.pin2, R4.Pin_0
  N14: Disp2.pin_3, R2.Pin_0
  N15: Disp2.pin_4, U2.Q4
  N16: Disp2.pin_5, R7.Pin_0
  N17: Disp2.pin_6, U2.Q6
  N18: Disp2.pin_7, R1.Pin_0
  N19: Disp2.pin_8, R0.Pin_0
  N20: Disp2.pin_9, U2.Q3
  N21: Disp2.pin_10, U2.Q1
  N22: Disp2.pin_11, R6.Pin_0
  N23: Disp2.pin_12, R5.Pin_0
  N24: Disp2.pin_13, U2.Q0
  N25: Disp2.pin_14, R3.Pin_0
  N26: Disp2.pin_15, U2.Q2
  N27: Disp2.pin_16, U2.Q5
  N28: R6.Pin_1, U1.Q6
  N29: R3.Pin_1, U1.Q3
  N30: R7.Pin_1, U1.Q7
  N31: R1.Pin_1, U1.Q1
  N32: R5.Pin_1, U1.Q5
  N33: R4.Pin_1, U1.Q4
  N34: R2.Pin_1, U1.Q2
  N35: R0.Pin_1, U1.Q0
  N36: U1.DS, U2.Q7'
  N37: U2.GND, U2.OE

custom parts:
  Keypad Membran 4x4: Membrane Keypad 4x4 Matrix
